# Fritzing sketch VoiceModulator (saved by Fritzing 0.9.3b)
breadboards: 1

parts:
  U1 = POT [package=pot_mammoth]
  Part2 = TRRS 3.5mm Jack Breakout
  Part1 = Arduino Mega 2560 (Rev3)
  Part3 = OLED Monochrome 128x64 1.3 inch [part_number=938]
  KY1 = KY-038 Sound Sensor Module
  Keypad4x1 = Keypad Membran 4x4

nets:
  N1: U1.A, Part1.D5_PWM
  N2: U1.E, Part2.RING2, Part2.RING1, Part2.TIP
  GND: Part2.SLEEVE, Part1.GND, Part3.GND, KY1.G
  N3: Part1.A0, KY1.AO
  N4: Part1.D21/SCL, Part3.SCLK_SCK
  N5: Part1.D20/SDA, Part3.MOSI_SDA
  5V: Part1.5V, Part3.VIN, KY1.VCC
  N6: Part1.D3_PWM, KY1.D0
  N7: Part1.D4_PWM, Part3.RESET
  N8: Part1.D24, Keypad4x1.Pin1
  N9: Part1.D26, Keypad4x1.Pin2
  N10: Part1.D28, Keypad4x1.Pin3
  N11: Part1.D30, Keypad4x1.Pin4
  N12: Part1.D32, Keypad4x1.Pin5
  N13: Part1.D34, Keypad4x1.Pin6
  N14: Part1.D36, Keypad4x1.Pin7
  N15: Part1.D38, Keypad4x1.Pin8

custom parts:
  OLED Monochrome 128x64 1.3 inch: These displays are small, only about 1.3" diagonal, but very readable due to the high contrast of an OLED display. This display is made of 128x64 individual white OLED pixels, each one is turned on or off by the controller chip. Because the display makes its own light, no backlight is required. This reduces the power required to run the OLED and is why the display has such high contrast; we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
  Keypad Membran 4x4: Membrane Keypad 4x4 Matrix
